// Digital circuit CORE.dig as structural Verilog
module CORE (
  input  clk
);

  wire ALUD_FLAG, ALUD_OE, ALUS_OE, BR_Q, button_2_out, CLK_t, CLR, comparator_1_eq, comparator_1_gt,
       comparator_1_lt, DC_JUMP, IMMED_OE, IRQ_OE, PSWF_OE, RAM_OE, RAM_WE, RF_HWE, RF_LWE, ROM_OE, SR_WE,
       WR_WE, XRAM_OE;
  wire [2:0] BR_SRC, BUS_SRC, JUMP_TYPE;
  wire [3:0] ALUSD_FUNC, RF_SRC;
  wire [7:0] DBUS, IMMED, RF_Q, SR_q, WR_q;
  wire [11:0] ADDRESS, dcouter_1_q;
  wire [47:42] DECODER_d;

  Comparator #(.Bits(8)) comparator_1 (
    .a(RF_Q), .b(IMMED), .gt(comparator_1_gt), .eq(comparator_1_eq), .lt(comparator_1_lt));
  DCOUTER dcouter_1 (.CLK(CLK_t), .nCLR(CLR), .CNT(1'b1), .nLE(DC_JUMP), .D(ADDRESS), .Q(dcouter_1_q));
  Multiplexer #(.Selector_Bits(3)) multiplexer_1 (
    .sel(JUMP_TYPE), .in_0(1'b0), .in_1(1'b1), .in_2(comparator_1_gt), .in_3(comparator_1_eq),
    .in_4(comparator_1_lt), .in_5(BR_Q), .in_6(1'b0), .in_7(1'b0), .out(DC_JUMP));
  Button button_1 (.out(CLR));
  Button button_2 (.out(button_2_out));
  ROM #(.AddrBits(12), .Bits(48)) DECODER (
    .A(dcouter_1_q), .sel(1'b1),
    .D({DECODER_d, IMMED, ADDRESS, JUMP_TYPE, ALUSD_FUNC, RAM_WE, BR_SRC, SR_WE, WR_WE, BUS_SRC, RF_HWE, RF_LWE, RF_SRC}));
  // SwitchDT switchdt_1: pin names not known; wires that end beside it: clk, button_2_out, CLK_t
  Decoder #(.Selector_Bits(3)) decoder_2 (
    .sel(BUS_SRC), .out_0(PSWF_OE), .out_1(ALUS_OE), .out_2(ALUD_OE), .out_3(IMMED_OE), .out_4(RAM_OE),
    .out_5(XRAM_OE), .out_6(ROM_OE), .out_7(IRQ_OE));
  // Probe on RF_SRC
  // Probe on RF_LWE
  // Probe on RF_HWE
  // Probe on BUS_SRC
  // Probe on WR_WE
  // Probe on SR_WE
  // Probe on BR_SRC
  // Probe on RAM_WE
  // Probe on ALUSD_FUNC
  // Probe on JUMP_TYPE
  // Probe on ADDRESS
  // Probe on IMMED
  // Probe on DBUS
  PullDown #(.Bits(8)) pulldown_1 (.out(DBUS));
  reg_file RF (.CLK(CLK_t), .RS(RF_SRC), .D(DBUS), .LLE(RF_LWE), .HLE(RF_HWE), .Q(RF_Q));
  // Probe on RF_Q
  BR BR (.C(CLK_t), .R(CLR), .S(BR_SRC), .ALUDF(ALUD_FLAG), .ALUSF(ALUD_FLAG), .A0(RF_Q[0]), .A7(RF_Q[7]), .Q(BR_Q));
  reg8clr WR (.D(DBUS), .CLK(CLK_t), .CLR(CLR), .LE(WR_WE), .Q(WR_q));
  reg8clr SR (.D(DBUS), .CLK(CLK_t), .CLR(CLR), .LE(SR_WE), .Q(SR_q));
  // Probe on WR_q
  // Probe on SR_q
  // Probe on {SR_q, WR_q}
  assign DBUS = IMMED_OE ? IMMED : 8'bz;  // Driver driver_1
  ALU ALU (
    .A(RF_Q), .B(WR_q), .S(ALUSD_FUNC), .CI(BR_Q), .nSOE(ALUS_OE), .DLOE(ALUD_OE), .DHOE(PSWF_OE), .O(DBUS),
    .CO(ALUD_FLAG));
  ROM #(.AddrBits(16), .Bits(8)) ROM (.A({SR_q, WR_q}), .sel(ROM_OE), .D(DBUS));
  RAMSinglePortSel #(.AddrBits(7), .Bits(8)) RAM (.A(SR_q[6:0]), .CS(SR_q[7]), .WE(RAM_WE), .OE(RAM_OE), .D(DBUS));

  // Notes on the sheet:
  //   contents of DECODER (hex, n*v repeats v):
  //   2880,18073,248,449,1ba,1ac0,2a8b8,290b9,2002220000a,30012e0000a,3800ae0000a,3c006e0000a,
  //   3e00520000a,3f00460000a,3f80420000a,3fc0420000a,3f40460000a,3e804e0000a,3ec04e0000a,
  //   3e40520000a,3d00620000a,3d805e0000a,3dc05e0000a,3d40620000a,3c806a0000a,3cc06a0000a,
  //   3c406e0000a,3a008e0000a,3b00820000a,3b807e0000a,3bc07e0000a,3b40820000a,3a808a0000a,
  //   3ac08a0000a,3a408e0000a,39009e0000a,39809a0000a,39c09a0000a,39409e0000a,3880a60000a,
  //   38c0a60000a,3840ae0000a,44480248,3400ee0000a,3600d20000a,3700c60000a,3780c20000a,
  //   37c0c20000a,3740c60000a,3680ce0000a,36c0ce0000a,3640d20000a,3500e20000a,3580de0000a,
  //   35c0de0000a,3540e20000a,3480ea0000a,34c0ea0000a,3440ee0000a,32010e0000a,3301020000a,
  //   3380fe0000a,33c0fe0000a,3341020000a,32810a0000a,32c10a0000a,32410e0000a,31011e0000a,
  //   31811a0000a,31c11a0000a,31411e0000a,3081260000a,30c1260000a,30412e0000a,44480248,
  //   2801c20000a,2c01720000a,2e01560000a,2f014a0000a,2f81460000a,2fc1460000a,2f414a0000a,
  //   2e81520000a,2ec1520000a,2e41560000a,2d01660000a,2d81620000a,2dc1620000a,2d41660000a,
  //   2c816e0000a,2cc16e0000a,2c41720000a,2a01920000a,2b01860000a,2b81820000a,2bc1820000a,
  //   2b41860000a,2a818e0000a,2ac18e0000a,2a41920000a,2901a20000a,29819e0000a,29c19e0000a,
  //   2941a20000a,2881ba0000a,28c1ba0000a,10c0,2a834,29035,46080000,2841c20000a,44480248,
  //   2401e20000a,2601ca0000a,2501d60000a,2581d20000a,2541d60000a,2481de0000a,24c1de0000a,
  //   2441e20000a,2202020000a,2301f60000a,2381f20000a,23c1f20000a,2341f60000a,2281fe0000a,
  //   22c1fe0000a,2242020000a,2102120000a,21820e0000a,21c20e0000a,2142120000a,20821a0000a,
  //   20c21a0000a,2042220000a,44480248,10032a0000a,1802aa0000a,1c026a0000a,1e024e0000a,
  //   1f02420000a,1f823e0000a,1fc23e0000a,1f42420000a,1e824a0000a,1ec24a0000a,1e424e0000a,
  //   1d025e0000a,1d825a0000a,1dc25a0000a,1d425e0000a,1c82660000a,1cc2660000a,1c426a0000a,
  //   1a028a0000a,1b027e0000a,1b827a0000a,1bc27a0000a,1b427e0000a,1a82860000a,1ac2860000a,
  //   1a428a0000a,19029a0000a,1982960000a,19c2960000a,19429a0000a,1882a20000a,18c2a20000a,
  //   1842aa0000a,44480248,1402ea0000a,1602ce0000a,1702c20000a,1782be0000a,17c2be0000a,
  //   1742c20000a,1682ca0000a,16c2ca0000a,1642ce0000a,1502de0000a,1582da0000a,15c2da0000a,
  //   1542de0000a,1482e60000a,14c2e60000a,1442ea0000a,12030a0000a,1302fe0000a,1382fa0000a,
  //   13c2fa0000a,1342fe0000a,1283060000a,12c3060000a,12430a0000a,11031a0000a,1183160000a,
  //   11c3160000a,11431a0000a,1083220000a,10c3220000a,10432a0000a,44480248,803ae0000a,c036e0000a,
  //   e03520000a,f03460000a,f83420000a,fc3420000a,f43460000a,e834e0000a,ec34e0000a,e43520000a,
  //   d03620000a,d835e0000a,dc35e0000a,d43620000a,c836a0000a,cc36a0000a,c436e0000a,a038e0000a,
  //   b03820000a,b837e0000a,bc37e0000a,b43820000a,a838a0000a,ac38a0000a,a438e0000a,9039e0000a,
  //   9839a0000a,9c39a0000a,9439e0000a,883aa0000a,8c3aa0000a,44480248,843ae0000a,403ee0000a,
  //   603d20000a,703c60000a,783c20000a,7c3c20000a,743c60000a,683ce0000a,6c3ce0000a,643d20000a,
  //   503e20000a,583de0000a,5c3de0000a,543e20000a,483ea0000a,4c3ea0000a,443ee0000a,2040e0000a,
  //   304020000a,383fe0000a,3c3fe0000a,344020000a,2840a0000a,2c40a0000a,2440e0000a,104220000a,
  //   1841a0000a,1c41a0000a,1441e0000a,40070,843e0000a,c42e0000a,20070,278,478,1bc,460801bc,
  //   44620000a,248,449,1bc,2a838,2a839,24c,180b8,24a,200002003c6,1803c,40020000c,400bc,
  //   24b,180bd,180be,402bd,124c,3280d,49280000,80000,482bc,100000,40472,4048,40472,4049,
  //   c000002c0,200bc,980b8
endmodule
